# Fritzing sketch iot-home_automation (saved by Fritzing 0.9.2b)
circuit board: 8.46667cm x 5.64444cm
breadboards: 1

parts:
  Part1 = Arduino Uno (Rev3)
  LED1 = smd LED [color="White (4500K)" package="1206 [SMD]"]
  M1 = DC Motor
  J1 = Piezo Speaker

nets:
  N1: Part1.A0, LED1.anode
  N2: Part1.A1, M1.pin_1
  N3: Part1.A2, J1.pin2
  N4: Part1.GND, LED1.cathode, M1.pin_2, J1.pin1
