# Fritzing sketch footlights (saved by Fritzing 0.9.2b)
breadboards: 1

parts:
  Part1 = Arduino Uno (Rev3)
  LPD8806_RGB_LED_Strip1 = LPD8806 RGB LED Strip
  J1 = Infrared Proximity Sensor

nets:
  N1: Part1.A0, J1.Vout
  N2: Part1.A1, LPD8806_RGB_LED_Strip1.+5V
  GND: Part1.GND, LPD8806_RGB_LED_Strip1.GND, J1.GND
  5V: Part1.5V, J1.Vcc

custom parts:
  LPD8806 RGB LED Strip: Digitally addressable RGB LED strip
