# Fritzing sketch reminder (saved by Fritzing 0.9.2b)
circuit board: 8.46667cm x 5.64444cm
breadboards: 1

parts:
  Part1 = Arduino Uno (Rev3)
  LED1 = LED - 3mm [color="Red (633nm)" package="3 mm [THT]"]
  LED2 = LED - 3mm [color="Yellow (595nm)" package="3 mm [THT]"]
  LED3 = LED - 3mm [color="Green (555nm)" package="3 mm [THT]"]

nets:
  N1: Part1.A0, LED2.anode
  N2: Part1.A1, LED1.anode
  N3: Part1.A2, LED3.anode
  N4: Part1.GND, LED1.cathode, LED2.cathode, LED3.cathode
