# Fritzing sketch obstacle_stick (saved by Fritzing 0.9.2b)
circuit board: 8.46667cm x 5.64444cm
breadboards: 1

parts:
  Part2 = Arduino Uno (Rev3)
  J2 = Infrared Proximity Sensor
  LED1 = smd LED [color="Red (633nm)" package="1206 [SMD]"]
  LED2 = smd LED [color="Green (555nm)" package="1206 [SMD]"]
  J3 = Piezo Speaker

nets:
  N1: Part2.A0, J2.Vout
  N2: Part2.A3, J3.pin2
  N3: Part2.A4/SDA, LED1.anode
  5V: Part2.5V, J2.Vcc
  GND: Part2.GND, J2.GND, LED2.cathode
